// Logisim project regfile-test.circ as structural Verilog: 1 circuit, main circuit main
module main (
  output [7:0] test_num,
  output [31:0] Reg_0_Value,
  output [31:0] Reg_1_Value,
  output [31:0] Reg_2_Value,
  output [31:0] Reg_3_Value,
  output [31:0] Read_Data_1,
  output [31:0] Read_Data_2
);

  wire clock_1_out;
  wire [7:0] adder_1_out;
  wire [15:0] rom_2_data;
  wire [31:0] WriteData;

  Register #(.width(8), .trigger("rising"), .Select("low")) register_1 (
    .D(adder_1_out), .en(1'b1), .Q(test_num), .clk(clock_1_out));  // open: clr
  Adder #(.width(8)) adder_1 (.a(8'h1), .b(test_num), .out(adder_1_out));  // open: cin, cout
  ROM #(.addrWidth(8), .dataWidth(32), .Select("high")) rom_1 (.addr(test_num), .data(WriteData));
  ROM #(.addrWidth(8), .dataWidth(16), .Select("high")) rom_2 (.addr(test_num), .data(rom_2_data), .sel(1'b1));
  Clock #(.highDuration(1), .lowDuration(1)) clock_1 (.out(clock_1_out));
  MIPS_Regfile mips_regfile_1 (
    .Reg1_num(rom_2_data[4:0]), .Reg2(rom_2_data[9:5]), .Write_Reg_num(rom_2_data[14:10]), .Din(WriteData),
    .Write_Enable(rom_2_data[15]), .Clock(clock_1_out), .Reg1Out(Read_Data_1), .Reg2Out(Read_Data_2),
    ._0_Value(Reg_0_Value), ._1_Value(Reg_1_Value), ._2_Value(Reg_2_Value), ._3_Value(Reg_3_Value));

  // Notes on the sheet:
  //   contents of rom_1 (hex, n*v repeats v):
  //   ffffffff 11111111 aaaaaaaa bbbbbbbb 66666666
  //   contents of rom_2 (hex, n*v repeats v):
  //   820 8462 8061 8c40 423
  //   图中不应该有蓝色或红色线缆，也不应该出现未知状态 x.
  //   你的寄存器文件封装正好合适放在这里
endmodule
