// Logisim project alu.circ as structural Verilog: 9 circuits, main circuit ☆ALU
// FA
module \一位全加器FA封装1  (
  input  Cin,
  input  Xi,
  input  Yi,
  output Cout,
  output Si
);

  wire AND_2_out, AND_out, XOR_2_out;

  or OR (Cout, AND_out, AND_2_out);
  and AND (AND_out, Xi, Yi);
  and AND_2 (AND_2_out, Cin, XOR_2_out);
  xor XOR (Si, Cin, XOR_2_out);
  xor XOR_2 (XOR_2_out, Xi, Yi);

  // Notes on the sheet:
  //   Si = Xi ^ Yi ^ Cin
  //   Cout = Xi Yi + Cin (Xi ^ Yi)
endmodule

// ADD
module \_8位串行加法器  (
  input  [7:0] X,
  input  [7:0] Y,
  input  Cin,
  output [7:0] S,
  output Cout,
  output Overflow
);

  wire \一位全加器fa封装1_2_cout , \一位全加器fa封装1_3_cout , \一位全加器fa封装1_4_cout , \一位全加器fa封装1_5_cout ,
       \一位全加器fa封装1_6_cout , \一位全加器fa封装1_7_cout , \一位全加器fa封装1_8_cout ;

  xor xor_1 (Overflow, Cout, \一位全加器fa封装1_2_cout );
  \一位全加器FA封装1  \u_一位全加器fa封装1_1  (.Cout(Cout), .Si(S[7]), .Cin(\一位全加器fa封装1_2_cout ), .Xi(X[7]), .Yi(Y[7]));
  \一位全加器FA封装1  \u_一位全加器fa封装1_2  (
    .Cout(\一位全加器fa封装1_2_cout ), .Si(S[6]), .Cin(\一位全加器fa封装1_3_cout ), .Xi(X[6]), .Yi(Y[6]));
  \一位全加器FA封装1  \u_一位全加器fa封装1_3  (
    .Cout(\一位全加器fa封装1_3_cout ), .Si(S[5]), .Cin(\一位全加器fa封装1_4_cout ), .Xi(X[5]), .Yi(Y[5]));
  \一位全加器FA封装1  \u_一位全加器fa封装1_4  (
    .Cout(\一位全加器fa封装1_4_cout ), .Si(S[4]), .Cin(\一位全加器fa封装1_5_cout ), .Xi(X[4]), .Yi(Y[4]));
  \一位全加器FA封装1  \u_一位全加器fa封装1_5  (
    .Cout(\一位全加器fa封装1_5_cout ), .Si(S[3]), .Cin(\一位全加器fa封装1_6_cout ), .Xi(X[3]), .Yi(Y[3]));
  \一位全加器FA封装1  \u_一位全加器fa封装1_6  (
    .Cout(\一位全加器fa封装1_6_cout ), .Si(S[2]), .Cin(\一位全加器fa封装1_7_cout ), .Xi(X[2]), .Yi(Y[2]));
  // Probe on X
  // Probe on Y
  // Probe on S
  \一位全加器FA封装1  \u_一位全加器fa封装1_7  (
    .Cout(\一位全加器fa封装1_7_cout ), .Si(S[1]), .Cin(\一位全加器fa封装1_8_cout ), .Xi(X[1]), .Yi(Y[1]));
  // Probe on X
  // Probe on Y
  // Probe on S
  \一位全加器FA封装1  \u_一位全加器fa封装1_8  (.Cout(\一位全加器fa封装1_8_cout ), .Si(S[0]), .Cin(Cin), .Xi(X[0]), .Yi(Y[0]));

  // Other names for the same wires on the sheet: OF = Overflow

  // Notes on the sheet:
  //   输入引脚区
  //   符号位
  //   输出引脚区
  //   +
  //   =
  //   有符号加法
  //   +
  //   =
  //   无符号加法
endmodule

// CAS
module \_8位串行可控加减法器  (
  input  [7:0] X,
  input  [7:0] Y,
  input  Cin,
  input  Sub,
  output [7:0] S,
  output Cout,
  output Overflow
);

  wire xor_2_out, xor_3_out, xor_4_out, xor_5_out, xor_6_out, xor_7_out, xor_8_out, xor_9_out,
       \一位全加器fa封装1_2_cout , \一位全加器fa封装1_3_cout , \一位全加器fa封装1_4_cout , \一位全加器fa封装1_5_cout ,
       \一位全加器fa封装1_6_cout , \一位全加器fa封装1_7_cout , \一位全加器fa封装1_8_cout ;
  wire [8:0] C;

  xor xor_1 (Overflow, Cout, \一位全加器fa封装1_2_cout );
  \一位全加器FA封装1  \u_一位全加器fa封装1_1  (.Cout(Cout), .Si(S[7]), .Cin(\一位全加器fa封装1_2_cout ), .Xi(X[7]), .Yi(xor_2_out));
  xor xor_2 (xor_2_out, Y[7], Sub);
  \一位全加器FA封装1  \u_一位全加器fa封装1_2  (
    .Cout(\一位全加器fa封装1_2_cout ), .Si(S[6]), .Cin(\一位全加器fa封装1_3_cout ), .Xi(X[6]), .Yi(xor_3_out));
  xor xor_3 (xor_3_out, Y[6], Sub);
  \一位全加器FA封装1  \u_一位全加器fa封装1_3  (
    .Cout(\一位全加器fa封装1_3_cout ), .Si(S[5]), .Cin(\一位全加器fa封装1_4_cout ), .Xi(X[5]), .Yi(xor_4_out));
  xor xor_4 (xor_4_out, Y[5], Sub);
  \一位全加器FA封装1  \u_一位全加器fa封装1_4  (
    .Cout(\一位全加器fa封装1_4_cout ), .Si(S[4]), .Cin(\一位全加器fa封装1_5_cout ), .Xi(X[4]), .Yi(xor_5_out));
  xor xor_5 (xor_5_out, Y[4], Sub);
  \一位全加器FA封装1  \u_一位全加器fa封装1_5  (
    .Cout(\一位全加器fa封装1_5_cout ), .Si(S[3]), .Cin(\一位全加器fa封装1_6_cout ), .Xi(X[3]), .Yi(xor_6_out));
  xor xor_6 (xor_6_out, Y[3], Sub);
  \一位全加器FA封装1  \u_一位全加器fa封装1_6  (
    .Cout(\一位全加器fa封装1_6_cout ), .Si(S[2]), .Cin(\一位全加器fa封装1_7_cout ), .Xi(X[2]), .Yi(xor_7_out));
  xor xor_7 (xor_7_out, Y[2], Sub);
  // Probe on X
  // Probe on Y
  // Probe on S
  \一位全加器FA封装1  \u_一位全加器fa封装1_7  (
    .Cout(\一位全加器fa封装1_7_cout ), .Si(S[1]), .Cin(\一位全加器fa封装1_8_cout ), .Xi(X[1]), .Yi(xor_8_out));
  xor xor_8 (xor_8_out, Y[1], Sub);
  \一位全加器FA封装1  \u_一位全加器fa封装1_8  (.Cout(\一位全加器fa封装1_8_cout ), .Si(S[0]), .Cin(Sub), .Xi(X[0]), .Yi(xor_9_out));
  xor xor_9 (xor_9_out, Y[0], Sub);
  // Probe on X
  // Probe on Y
  // Probe on S
  Multiplexer #(.select(1), .width(9), .disabled("Z"), .enable("false")) multiplexer_1 (
    .in0(9'hba), .in1(9'h92), .out(C), .sel(Sub));

  // Other names for the same wires on the sheet: OF = Overflow

  // Notes on the sheet:
  //   输入引脚区
  //   符号位
  //   输出引脚区
  //   =
  //   有符号
  //   =
  //   无符号
endmodule

// CLA74182
module CLA74182 (
  input  G4,
  input  P4,
  input  G3,
  input  P3,
  input  G2,
  input  P2,
  input  G1,
  input  P1,
  input  Cin,
  output C4,
  output C3,
  output C2,
  output C1,
  output G_star,
  output P_star
);

  wire and_2_out, and_3_out, and_4_out, and_5_out, and_6_out, and_7_out, and_8_out, and_9_out, and_10_out,
       and_11_out;

  and and_1 (P_star, P4, P3, P2, P1);
  or or_1 (G_star, and_4_out, and_3_out, and_2_out, G4);
  or or_2 (C4, G4, and_2_out, and_3_out, and_4_out, and_5_out);
  and and_2 (and_2_out, P4, G3);
  and and_3 (and_3_out, P4, P3, G2);
  and and_4 (and_4_out, P4, P3, P2, G1);
  or or_3 (C3, G3, and_6_out, and_7_out, and_8_out);
  and and_5 (and_5_out, P4, P3, P2, P1, Cin);
  and and_6 (and_6_out, P3, G2);
  and and_7 (and_7_out, P3, P2, G1);
  and and_8 (and_8_out, P3, P2, P1, Cin);
  or or_4 (C1, G1, and_11_out);
  or or_5 (C2, G2, and_9_out, and_10_out);
  and and_9 (and_9_out, P2, G1);
  and and_10 (and_10_out, P2, P1, Cin);
  and and_11 (and_11_out, P1, Cin);

  // Notes on the sheet:
  //   输入引脚区
  //   请根据以上引脚以及隧道信号设计完成74LS182先行进位电路
  //   输出引脚区
  //   请勿增改引脚定义
  //   Pi=Xi^Yi
  //   Gi=XiYi
  //   Ci=XiYi+(Xi^Yi)Ci-1
  //   P*=P4P3P2P1
  //   G*=G4+P4G3+P4P3G2+P4P3P2G1
endmodule

// 4位快速加法器
module \_4位快速加法器  (
  input  [3:0] X,
  input  [3:0] Y,
  input  Cin,
  output [3:0] S,
  output Cout,
  output G_star,
  output P_star
);

  wire and_1_out, and_2_out, and_3_out, and_4_out, cla74182_1_c1, cla74182_1_c2, cla74182_1_c3, xor_1_out,
       xor_2_out, xor_3_out, xor_4_out;

  CLA74182 cla74182_1 (
    .G4(and_1_out), .P4(xor_1_out), .G3(and_2_out), .P3(xor_2_out), .G2(and_3_out), .P2(xor_3_out),
    .G1(and_4_out), .P1(xor_4_out), .Cin(Cin), .C4(Cout), .C3(cla74182_1_c3), .C2(cla74182_1_c2),
    .C1(cla74182_1_c1), .G_star(G_star), .P_star(P_star));
  and and_1 (and_1_out, Y[3], X[3]);
  xor xor_1 (xor_1_out, Y[3], X[3]);
  \一位全加器FA封装1  \u_一位全加器fa封装1_1  (.Si(S[3]), .Cin(cla74182_1_c3), .Xi(Y[3]), .Yi(X[3]));  // open: Cout
  xor xor_2 (xor_2_out, Y[2], X[2]);
  and and_2 (and_2_out, Y[2], X[2]);
  \一位全加器FA封装1  \u_一位全加器fa封装1_2  (.Si(S[2]), .Cin(cla74182_1_c2), .Xi(Y[2]), .Yi(X[2]));  // open: Cout
  xor xor_3 (xor_3_out, Y[1], X[1]);
  and and_3 (and_3_out, Y[1], X[1]);
  and and_4 (and_4_out, Y[0], X[0]);
  \一位全加器FA封装1  \u_一位全加器fa封装1_3  (.Si(S[1]), .Cin(cla74182_1_c1), .Xi(Y[1]), .Yi(X[1]));  // open: Cout
  xor xor_4 (xor_4_out, Y[0], X[0]);
  // Probe on X
  // Probe on Y
  // Probe on S
  \一位全加器FA封装1  \u_一位全加器fa封装1_4  (.Si(S[0]), .Cin(Cin), .Xi(Y[0]), .Yi(X[0]));  // open: Cout
  // Probe on X
  // Probe on Y
  // Probe on S

  // Notes on the sheet:
  //   输入引脚区
  //   输出引脚区
  //   +
  //   =
  //   有符号加法
  //   +
  //   =
  //   无符号加法
endmodule

// 16位快速加法器
module \_16位快速加法器  (
  input  [15:0] X,
  input  [15:0] Y,
  input  Cin,
  output [15:0] S,
  output Cout,
  output G_star,
  output P_star
);

  wire cla74182_1_c1, cla74182_1_c2, cla74182_1_c3, \n4位快速加法器_1_g_star , \n4位快速加法器_1_p_star ,
       \n4位快速加法器_2_g_star , \n4位快速加法器_2_p_star , \n4位快速加法器_3_g_star , \n4位快速加法器_3_p_star ,
       \n4位快速加法器_4_g_star , \n4位快速加法器_4_p_star ;

  CLA74182 cla74182_1 (
    .G4(\n4位快速加法器_1_g_star ), .P4(\n4位快速加法器_1_p_star ), .G3(\n4位快速加法器_2_g_star ), .P3(\n4位快速加法器_2_p_star ),
    .G2(\n4位快速加法器_3_g_star ), .P2(\n4位快速加法器_3_p_star ), .G1(\n4位快速加法器_4_g_star ), .P1(\n4位快速加法器_4_p_star ),
    .Cin(Cin), .C4(Cout), .C3(cla74182_1_c3), .C2(cla74182_1_c2), .C1(cla74182_1_c1), .G_star(G_star),
    .P_star(P_star));
  \_4位快速加法器  \u_4位快速加法器_1  (
    .X(X[15:12]), .Y(Y[15:12]), .Cin(cla74182_1_c3), .S(S[15:12]), .G_star(\n4位快速加法器_1_g_star ),
    .P_star(\n4位快速加法器_1_p_star ));  // open: Cout
  \_4位快速加法器  \u_4位快速加法器_2  (
    .X(X[11:8]), .Y(Y[11:8]), .Cin(cla74182_1_c2), .S(S[11:8]), .G_star(\n4位快速加法器_2_g_star ),
    .P_star(\n4位快速加法器_2_p_star ));  // open: Cout
  \_4位快速加法器  \u_4位快速加法器_3  (
    .X(X[7:4]), .Y(Y[7:4]), .Cin(cla74182_1_c1), .S(S[7:4]), .G_star(\n4位快速加法器_3_g_star ),
    .P_star(\n4位快速加法器_3_p_star ));  // open: Cout
  // Probe on X
  // Probe on Y
  // Probe on S
  // Probe on X
  // Probe on Y
  // Probe on S
  \_4位快速加法器  \u_4位快速加法器_4  (
    .X(X[3:0]), .Y(Y[3:0]), .Cin(Cin), .S(S[3:0]), .G_star(\n4位快速加法器_4_g_star ), .P_star(\n4位快速加法器_4_p_star ));  // open: Cout

  // Other names for the same wires on the sheet: S0[3:0] = S[3:0]; S1[3:0] = S[7:4]; S2[3:0] = S[11:8];
  //   S3[3:0] = S[15:12]; X0[3:0] = X[3:0]; X1[3:0] = X[7:4]; X2[3:0] = X[11:8]; X3[3:0] = X[15:12]; Y0[3:0] = Y[3:0];
  //   Y1[3:0] = Y[7:4]; Y2[3:0] = Y[11:8]; Y3[3:0] = Y[15:12]

  // Notes on the sheet:
  //   输入引脚区
  //   输出引脚区
  //   +
  //   =
  //   有符号加法
  //   +
  //   =
  //   无符号加法
endmodule

// 32位加法器
module \_32位快速加法器  (
  input  Cin,
  input  [31:0] X,
  input  [31:0] Y,
  output Cout,
  output [31:0] S,
  output Overflow
);

  wire and_1_out, and_2_out, cla74182_1_c1, \n16位快速加法器_1_g_star , \n16位快速加法器_1_p_star , \n16位快速加法器_2_g_star ,
       \n16位快速加法器_2_p_star , not_1_out, not_2_out, not_3_out;

  or or_1 (Overflow, and_1_out, and_2_out);
  and and_1 (and_1_out, X[31], Y[31], not_3_out);
  not not_1 (not_1_out, X[31]);
  not not_2 (not_2_out, Y[31]);
  and and_2 (and_2_out, not_1_out, not_2_out, S[31]);
  CLA74182 cla74182_1 (
    .G4(1'b0), .P4(1'b0), .G3(1'b0), .P3(1'b0), .G2(\n16位快速加法器_1_g_star ), .P2(\n16位快速加法器_1_p_star ),
    .G1(\n16位快速加法器_2_g_star ), .P1(\n16位快速加法器_2_p_star ), .Cin(Cin), .C2(Cout), .C1(cla74182_1_c1));  // open: C4, C3, G_star, P_star
  not not_3 (not_3_out, S[31]);
  // Probe on X
  // Probe on Y
  // Probe on S
  \_16位快速加法器  \u_16位快速加法器_1  (
    .X(X[31:16]), .Y(Y[31:16]), .Cin(cla74182_1_c1), .S(S[31:16]), .G_star(\n16位快速加法器_1_g_star ),
    .P_star(\n16位快速加法器_1_p_star ));  // open: Cout
  // Probe on X
  // Probe on Y
  // Probe on S
  \_16位快速加法器  \u_16位快速加法器_2  (
    .X(X[15:0]), .Y(Y[15:0]), .Cin(Cin), .S(S[15:0]), .G_star(\n16位快速加法器_2_g_star ),
    .P_star(\n16位快速加法器_2_p_star ));  // open: Cout

  // Other names for the same wires on the sheet: S0[15:0] = S[15:0]; S1[15:0] = S[31:16]; X0[15:0] = X[15:0];
  //   X1[15:0] = X[31:16]; Y0[15:0] = Y[15:0]; Y1[15:0] = Y[31:16]

  // Notes on the sheet:
  //   输入引脚区
  //   输出引脚区
  //   +
  //   =
  //   有符号加法
  //   +
  //   =
  //   无符号加法
endmodule

// ALU
module ALU (
  input  [31:0] X,
  input  [31:0] Y,
  input  [3:0] AluOP,
  output Signed_Overflow,
  output UnSigned_Overflow,
  output Equal,
  output [31:0] Result,
  output [31:0] Result_2
);

  wire comparator_1_lt, comparator_2_lt, \n32位快速加法器_1_cout , \n32位快速加法器_1_overflow , \n32位快速加法器_2_overflow ;
  wire [31:0] and_1_out, bit_extender_1_out, bit_extender_2_out, divider_1_out, divider_1_rem,
       multiplier_1_cout, multiplier_1_out, \n32位快速加法器_1_s , \n32位快速加法器_2_s , negator_1_out, nor_1_out,
       or_1_out, shifter_1_out, shifter_2_out, shifter_3_out, xor_1_out;

  // Probe on X
  // Probe on X
  // Probe on Y
  // Probe on Y
  Negator #(.width(32)) negator_1 (.in(Y), .out(negator_1_out));
  \_32位快速加法器  \u_32位快速加法器_1  (
    .X(X), .Y(Y), .Cin(1'b0), .S(\n32位快速加法器_1_s ), .Cout(\n32位快速加法器_1_cout ),
    .Overflow(\n32位快速加法器_1_overflow ));
  \_32位快速加法器  \u_32位快速加法器_2  (
    .X(X), .Y(negator_1_out), .Cin(1'b0), .S(\n32位快速加法器_2_s ), .Overflow(\n32位快速加法器_2_overflow ));  // open: Cout
  // Probe on AluOP
  // Probe on Result
  // Probe on Result
  Shifter #(.width(32), .shift("ll")) shifter_1 (.in(X), .\dist (Y[4:0]), .out(shifter_1_out));
  Shifter #(.width(32), .shift("ar")) shifter_2 (.in(X), .\dist (Y[4:0]), .out(shifter_2_out));
  Shifter #(.width(32), .shift("lr")) shifter_3 (.in(X), .\dist (Y[4:0]), .out(shifter_3_out));
  Multiplier #(.width(32)) multiplier_1 (
    .a(X), .b(Y), .out(multiplier_1_out), .cin({32{1'b0}}), .cout(multiplier_1_cout));
  Divider #(.width(32)) divider_1 (.a(X), .b(Y), .out(divider_1_out), .upper({32{1'b0}}), .rem(divider_1_rem));
  assign and_1_out = X & Y;  // AND_Gate and_1, 32 bits wide
  assign or_1_out = X | Y;  // OR_Gate or_1, 32 bits wide
  assign xor_1_out = X ^ Y;  // XOR_Gate xor_1, 32 bits wide
  assign nor_1_out = ~(X | Y);  // NOR_Gate nor_1, 32 bits wide
  Comparator #(.width(32), .mode("twosComplement")) comparator_1 (.a(X), .b(Y), .lt(comparator_1_lt));  // open: gt, eq
  Comparator #(.width(32), .mode("unsigned")) comparator_2 (.a(X), .b(Y), .lt(comparator_2_lt));  // open: gt, eq
  Comparator #(.width(32), .mode("unsigned")) comparator_3 (.a(X), .b(Y), .eq(Equal));  // open: gt, lt
  // Probe on Result_2
  assign bit_extender_1_out = {{31{1'b0}}, comparator_1_lt};  // Bit_Extender bit_extender_1
  assign bit_extender_2_out = {{31{1'b0}}, comparator_2_lt};  // Bit_Extender bit_extender_2
  Multiplexer #(.select(4), .width(32), .disabled("Z"), .enable("false")) multiplexer_1 (
    .in0(shifter_1_out), .in1(shifter_2_out), .in2(shifter_3_out), .in3(multiplier_1_out),
    .in4(divider_1_out), .in5(\n32位快速加法器_1_s ), .in6(\n32位快速加法器_2_s ), .in7(and_1_out), .in8(or_1_out),
    .in9(xor_1_out), .in10(nor_1_out), .in11(bit_extender_1_out), .in12(bit_extender_2_out),
    .in13({32{1'b0}}), .in14({32{1'b0}}), .in15({32{1'b0}}), .out(Result), .sel(AluOP));
  Multiplexer #(.select(4), .width(32), .disabled("Z"), .enable("false")) multiplexer_2 (
    .in0({32{1'b0}}), .in1({32{1'b0}}), .in2({32{1'b0}}), .in3(multiplier_1_cout), .in4(divider_1_rem),
    .in5({32{1'b0}}), .in6({32{1'b0}}), .in7({32{1'b0}}), .in8({32{1'b0}}), .in9({32{1'b0}}),
    .in10({32{1'b0}}), .in11({32{1'b0}}), .in12({32{1'b0}}), .in13({32{1'b0}}), .in14({32{1'b0}}),
    .in15({32{1'b0}}), .out(Result_2), .sel(AluOP));
  Multiplexer #(.select(4), .width(1), .disabled("Z"), .enable("false")) multiplexer_3 (
    .in0(1'b0), .in1(1'b0), .in2(1'b0), .in3(1'b0), .in4(1'b0), .in5(\n32位快速加法器_1_overflow ),
    .in6(\n32位快速加法器_2_overflow ), .in7(1'b0), .in8(1'b0), .in9(1'b0), .in10(1'b0), .in11(1'b0), .in12(1'b0),
    .in13(1'b0), .in14(1'b0), .in15(1'b0), .out(Signed_Overflow), .sel(AluOP));
  Multiplexer #(.select(4), .width(1), .disabled("Z"), .enable("false")) multiplexer_4 (
    .in0(1'b0), .in1(1'b0), .in2(1'b0), .in3(1'b0), .in4(1'b0), .in5(\n32位快速加法器_1_cout ),
    .in6(comparator_2_lt), .in7(1'b0), .in8(1'b0), .in9(1'b0), .in10(1'b0), .in11(1'b0), .in12(1'b0),
    .in13(1'b0), .in14(1'b0), .in15(1'b0), .out(UnSigned_Overflow), .sel(AluOP));

  // Other names for the same wires on the sheet: OF = Signed_Overflow; Result2[31:0] = Result_2; S[3:0] = AluOP;
  //   UOF = UnSigned_Overflow

  // Notes on the sheet:
  //   不要改变此引脚区域内容，也不要改变ALU封装形式
  //   输入引脚
  //   请在下方利用上方输入输出引脚的隧道信号构建ALU电路，ctrl+d复制选择部件
  //   输出引脚
  //   探测区域
endmodule

module \运算器测试电路  (
  output Signed_Overflow,
  output Unsigned_overflow,
  output [31:0] Result,
  output Equal,
  output [31:0] Result_2
);

  wire clock_1_out, comparator_1_eq;
  wire [3:0] rom_3_data;
  wire [7:0] adder_1_out, register_1_q;
  wire [31:0] rom_1_data, rom_2_data, rom_4_data, rom_5_data;

  Clock #(.highDuration(1), .lowDuration(1)) clock_1 (.out(clock_1_out));
  Adder #(.width(8)) adder_1 (.a(8'h1), .b(register_1_q), .out(adder_1_out));  // open: cin, cout
  Register #(.width(8), .trigger("rising"), .Select("low")) register_1 (
    .D(adder_1_out), .Q(register_1_q), .clk(clock_1_out));  // open: en, clr
  // Probe on register_1_q
  // Probe on rom_1_data
  ROM #(.addrWidth(8), .dataWidth(32), .Select("high")) rom_1 (.addr(register_1_q), .data(rom_1_data));
  ROM #(.addrWidth(8), .dataWidth(32), .Select("high")) rom_2 (.addr(register_1_q), .data(rom_2_data));
  // Probe on rom_2_data
  ROM #(.addrWidth(8), .dataWidth(4), .Select("high")) rom_3 (.addr(register_1_q), .data(rom_3_data));
  ROM #(.addrWidth(8), .dataWidth(32), .Select("high")) rom_4 (.addr(register_1_q), .data(rom_4_data));
  ROM #(.addrWidth(8), .dataWidth(32), .Select("high")) rom_5 (.addr(register_1_q), .data(rom_5_data));
  ALU alu_1 (
    .AluOP(rom_3_data), .X(rom_1_data), .Equal(Equal), .Result(Result), .Signed_Overflow(Signed_Overflow),
    .Y(rom_2_data), .Result_2(Result_2), .UnSigned_Overflow(Unsigned_overflow));
  // Probe on rom_4_data
  // Probe on rom_5_data
  // Probe on Result
  // Probe on Result_2
  Comparator #(.width(32), .mode("twosComplement")) comparator_1 (
    .a(Result), .b(rom_4_data), .eq(comparator_1_eq));  // open: gt, lt
  Comparator #(.width(32), .mode("twosComplement")) comparator_2 (
    .a(Result_2), .b(rom_5_data), .eq(comparator_1_eq));  // open: gt, lt
  LED #(.active("true")) led_1 (.in(comparator_1_eq));

  // Notes on the sheet:
  //   contents of rom_1 (hex, n*v repeats v):
  //   10*123 6 fffffff8 fffffff8
  //   contents of rom_2 (hex, n*v repeats v):
  //   4*3 15 5*3 1 1 1
  //   contents of rom_3 (hex, n*v repeats v):
  //   0 1 2 3 4 5 6 7 8 9 a b c
  //   contents of rom_4 (hex, n*v repeats v):
  //   918 24 24 369 d 126 120 3 123 120 fffffff8 1
  //   contents of rom_5 (hex, n*v repeats v):
  //   4*0 12
  //   此电路用于检测学生设计的ALU部件封装是否符合要求
  //   当电路设计完成后，蓝色线红色不应该出现，输出也不应该是高阻态
  //   ROM中可以存放测试用例，使用时钟驱动调出不同的X，Y，S值进行批量验证
  //   封装的ALU应该正好放置于此
endmodule
